// Logisim project PRESENT.circ as structural Verilog
module S_box (
  input  [3:0] in_1,
  input  [3:0] in_2,
  input  [3:0] in_3,
  input  [3:0] in_4,
  input  [3:0] in_5,
  input  [3:0] in_6,
  input  [3:0] in_7,
  input  [3:0] in_8,
  input  [3:0] in_9,
  input  [3:0] in_10,
  input  [3:0] in_11,
  input  [3:0] in_12,
  input  [3:0] in_13,
  input  [3:0] in_14,
  input  [3:0] in_15,
  input  [3:0] in_16,
  output [3:0] out_17,
  output [3:0] out_18,
  output [3:0] out_19,
  output [3:0] out_20,
  output [3:0] out_21,
  output [3:0] out_22,
  output [3:0] out_23,
  output [3:0] out_24,
  output [3:0] out_25,
  output [3:0] out_26,
  output [3:0] out_27,
  output [3:0] out_28,
  output [3:0] out_29,
  output [3:0] out_30,
  output [3:0] out_31,
  output [3:0] out_32
);

  mini_Sbox s15 (.in_1(in_1), .out_2(out_17[3]), .out_3(out_17[2]), .out_4(out_17[1]), .out_5(out_17[0]));
  mini_Sbox s14 (.in_1(in_2), .out_2(out_18[3]), .out_3(out_18[2]), .out_4(out_18[1]), .out_5(out_18[0]));
  mini_Sbox s13 (.in_1(in_3), .out_2(out_19[3]), .out_3(out_19[2]), .out_4(out_19[1]), .out_5(out_19[0]));
  mini_Sbox s12 (.in_1(in_4), .out_2(out_20[3]), .out_3(out_20[2]), .out_4(out_20[1]), .out_5(out_20[0]));
  mini_Sbox s11 (.in_1(in_5), .out_2(out_21[3]), .out_3(out_21[2]), .out_4(out_21[1]), .out_5(out_21[0]));
  mini_Sbox s10 (.in_1(in_6), .out_2(out_22[3]), .out_3(out_22[2]), .out_4(out_22[1]), .out_5(out_22[0]));
  mini_Sbox s9 (.in_1(in_7), .out_2(out_23[3]), .out_3(out_23[2]), .out_4(out_23[1]), .out_5(out_23[0]));
  mini_Sbox s8 (.in_1(in_8), .out_2(out_24[3]), .out_3(out_24[2]), .out_4(out_24[1]), .out_5(out_24[0]));
  mini_Sbox s7 (.in_1(in_9), .out_2(out_25[3]), .out_3(out_25[2]), .out_4(out_25[1]), .out_5(out_25[0]));
  mini_Sbox s5 (.in_1(in_11), .out_2(out_27[3]), .out_3(out_27[2]), .out_4(out_27[1]), .out_5(out_27[0]));
  mini_Sbox s6 (.in_1(in_10), .out_2(out_26[3]), .out_3(out_26[2]), .out_4(out_26[1]), .out_5(out_26[0]));
  mini_Sbox s4 (.in_1(in_12), .out_2(out_28[3]), .out_3(out_28[2]), .out_4(out_28[1]), .out_5(out_28[0]));
  mini_Sbox s3 (.in_1(in_13), .out_2(out_29[3]), .out_3(out_29[2]), .out_4(out_29[1]), .out_5(out_29[0]));
  mini_Sbox s2 (.in_1(in_14), .out_2(out_30[3]), .out_3(out_30[2]), .out_4(out_30[1]), .out_5(out_30[0]));
  mini_Sbox s1 (.in_1(in_15), .out_2(out_31[3]), .out_3(out_31[2]), .out_4(out_31[1]), .out_5(out_31[0]));
  mini_Sbox s0 (.in_1(in_16), .out_2(out_32[3]), .out_3(out_32[2]), .out_4(out_32[1]), .out_5(out_32[0]));
endmodule

module mini_Sbox (
  input  [3:0] in_1,
  output out_2,
  output out_3,
  output out_4,
  output out_5
);

  y3_n y3 (.a(in_1[3]), .b(in_1[2]), .c(in_1[1]), .d(in_1[0]), .x(out_2));
  y2_n y2 (.a(in_1[3]), .b(in_1[2]), .c(in_1[1]), .d(in_1[0]), .x(out_3));
  y1_n y1 (.a(in_1[3]), .b(in_1[2]), .c(in_1[1]), .d(in_1[0]), .x(out_4));
  y0_n y0 (.a(in_1[3]), .b(in_1[2]), .c(in_1[1]), .d(in_1[0]), .x(out_5));
endmodule

module y0_n (
  input  a,
  input  b,
  input  c,
  input  d,
  output x
);

  wire and_1_out, and_2_out, and_3_out, and_4_out, and_5_out, and_6_out, not_1_out, not_2_out, not_3_out,
       not_4_out, not_5_out, not_6_out, not_7_out, not_8_out, not_9_out, not_10_out;

  not not_1 (not_1_out, c);
  not not_2 (not_2_out, b);
  not not_3 (not_3_out, d);
  not not_4 (not_4_out, d);
  not not_5 (not_5_out, a);
  not not_6 (not_6_out, b);
  not not_7 (not_7_out, a);
  not not_8 (not_8_out, a);
  not not_9 (not_9_out, c);
  not not_10 (not_10_out, d);
  and and_1 (and_1_out, a, b, not_1_out, d);
  and and_2 (and_2_out, a, not_2_out, not_3_out);
  and and_3 (and_3_out, a, c, not_4_out);
  and and_4 (and_4_out, not_5_out, not_6_out, d);
  and and_5 (and_5_out, not_7_out, c, d);
  and and_6 (and_6_out, not_8_out, b, not_9_out, not_10_out);
  or or_1 (x, and_1_out, and_2_out, and_3_out, and_4_out, and_5_out, and_6_out);
endmodule

module y1_n (
  input  a,
  input  b,
  input  c,
  input  d,
  output x
);

  wire and_1_out, and_2_out, and_3_out, and_4_out, and_5_out, not_1_out, not_2_out, not_3_out, not_4_out,
       not_5_out, not_6_out, not_7_out;

  not not_1 (not_1_out, b);
  and and_1 (and_1_out, a, not_1_out, not_2_out);
  not not_2 (not_2_out, d);
  and and_2 (and_2_out, a, not_3_out, d);
  not not_3 (not_3_out, c);
  and and_3 (and_3_out, a, b, d);
  not not_4 (not_4_out, a);
  and and_4 (and_4_out, not_4_out, not_5_out, c);
  not not_5 (not_5_out, b);
  not not_6 (not_6_out, a);
  and and_5 (and_5_out, not_6_out, c, not_7_out);
  not not_7 (not_7_out, d);
  or or_1 (x, and_1_out, and_2_out, and_3_out, and_4_out, and_5_out);
endmodule

module y2_n (
  input  a,
  input  b,
  input  c,
  input  d,
  output x
);

  wire and_1_out, and_2_out, and_3_out, and_4_out, and_5_out, not_1_out, not_2_out, not_3_out, not_4_out,
       not_5_out, not_6_out, not_7_out, not_8_out;

  not not_1 (not_1_out, a);
  not not_2 (not_2_out, b);
  not not_3 (not_3_out, c);
  not not_4 (not_4_out, b);
  not not_5 (not_5_out, d);
  not not_6 (not_6_out, c);
  not not_7 (not_7_out, c);
  not not_8 (not_8_out, a);
  and and_1 (and_1_out, not_1_out, not_2_out, not_3_out);
  and and_2 (and_2_out, not_4_out, c, not_5_out);
  and and_3 (and_3_out, a, b, not_6_out);
  and and_4 (and_4_out, a, not_7_out, d);
  and and_5 (and_5_out, not_8_out, b, c, d);
  or or_1 (x, and_1_out, and_2_out, and_3_out, and_4_out, and_5_out);
endmodule

module y3_n (
  input  a,
  input  b,
  input  c,
  input  d,
  output x
);

  wire and_1_out, and_2_out, and_3_out, and_4_out, and_5_out, not_1_out, not_2_out, not_3_out, not_4_out,
       not_5_out, not_6_out, not_7_out;

  not not_1 (not_1_out, a);
  not not_2 (not_2_out, c);
  and and_1 (and_1_out, not_1_out, not_2_out, not_3_out);
  not not_3 (not_3_out, d);
  not not_4 (not_4_out, a);
  and and_2 (and_2_out, not_4_out, c, d);
  not not_5 (not_5_out, a);
  and and_3 (and_3_out, not_5_out, b, c);
  and and_4 (and_4_out, a, not_6_out, d);
  not not_6 (not_6_out, b);
  and and_5 (and_5_out, a, not_7_out, c);
  not not_7 (not_7_out, b);
  or or_1 (x, and_1_out, and_2_out, and_3_out, and_4_out, and_5_out);
endmodule

module P_box (
  input  [3:0] in_1,
  input  [3:0] in_2,
  input  [3:0] in_3,
  input  [3:0] in_4,
  input  [3:0] in_5,
  input  [3:0] in_6,
  input  [3:0] in_7,
  input  [3:0] in_8,
  input  [3:0] in_9,
  input  [3:0] in_10,
  input  [3:0] in_11,
  input  [3:0] in_12,
  input  [3:0] in_13,
  input  [3:0] in_14,
  input  [3:0] in_15,
  input  [3:0] in_16,
  output [3:0] p3,
  output [3:0] p2,
  output [3:0] p1,
  output [3:0] p0,
  output [3:0] p7,
  output [3:0] p6,
  output [3:0] p5,
  output [3:0] p4,
  output [3:0] p11,
  output [3:0] p10,
  output [3:0] p9,
  output [3:0] p8,
  output [3:0] p15,
  output [3:0] p14,
  output [3:0] p13,
  output [3:0] p12
);


  assign p0 = {in_13[0], in_14[0], in_15[0], in_16[0]};
  assign p1 = {in_9[0], in_10[0], in_11[0], in_12[0]};
  assign p2 = {in_5[0], in_6[0], in_7[0], in_8[0]};
  assign p3 = {in_1[0], in_2[0], in_3[0], in_4[0]};
  assign p4 = {in_13[1], in_14[1], in_15[1], in_16[1]};
  assign p5 = {in_9[1], in_10[1], in_11[1], in_12[1]};
  assign p6 = {in_5[1], in_6[1], in_7[1], in_8[1]};
  assign p7 = {in_1[1], in_2[1], in_3[1], in_4[1]};
  assign p8 = {in_13[2], in_14[2], in_15[2], in_16[2]};
  assign p9 = {in_9[2], in_10[2], in_11[2], in_12[2]};
  assign p10 = {in_5[2], in_6[2], in_7[2], in_8[2]};
  assign p11 = {in_1[2], in_2[2], in_3[2], in_4[2]};
  assign p12 = {in_13[3], in_14[3], in_15[3], in_16[3]};
  assign p13 = {in_9[3], in_10[3], in_11[3], in_12[3]};
  assign p14 = {in_5[3], in_6[3], in_7[3], in_8[3]};
  assign p15 = {in_1[3], in_2[3], in_3[3], in_4[3]};
endmodule
